// Logisim project SAAT.circ as structural Verilog
module SAAT (
);

  wire and_1_out, and_2_out, and_3_out, and_4_out, and_5_out, and_6_out, and_7_out, and_8_out, and_9_out,
       and_10_out, and_11_out, and_12_out, and_13_out, and_14_out, and_15_out, and_16_out, and_17_out,
       and_18_out, and_19_out, and_20_out, and_21_out, and_22_out, and_23_out, and_24_out, and_25_out,
       and_26_out, and_27_out, and_28_out, and_29_out, and_30_out, and_31_out, Clk_out, j_k_ff_1_q,
       j_k_ff_1_qn, j_k_ff_2_q, j_k_ff_2_qn, j_k_ff_3_q, j_k_ff_3_qn, j_k_ff_4_q, j_k_ff_4_qn, j_k_ff_5_q,
       j_k_ff_5_qn, j_k_ff_6_q, j_k_ff_6_qn, j_k_ff_7_q, j_k_ff_8_q, j_k_ff_9_q, j_k_ff_10_q, j_k_ff_11_q,
       j_k_ff_11_qn, j_k_ff_12_q, j_k_ff_12_qn, j_k_ff_13_q, j_k_ff_13_qn, j_k_ff_14_q, j_k_ff_14_qn,
       j_k_ff_15_q, j_k_ff_15_qn, j_k_ff_16_q, j_k_ff_16_qn, j_k_ff_17_q, j_k_ff_17_qn, or_1_out, or_2_out,
       or_3_out, or_4_out, xor_1_out, xor_2_out;

  and and_1 (and_1_out, j_k_ff_6_q, j_k_ff_5_q, j_k_ff_4_q, j_k_ff_2_q, j_k_ff_1_q);
  and and_2 (and_2_out, j_k_ff_6_q, j_k_ff_5_q, j_k_ff_4_q, j_k_ff_3_q);
  and and_3 (and_3_out, j_k_ff_1_q, j_k_ff_2_q);
  LED led_1 (.in(j_k_ff_1_q));
  J_K_Flip_Flop j_k_ff_1 (
    .J(1'b1), .clk(and_19_out), .K(1'b1), .Q(j_k_ff_1_q), .Qn(j_k_ff_1_qn), .reset(and_2_out));  // open: preset, en
  LED led_2 (.in(j_k_ff_2_q));
  J_K_Flip_Flop j_k_ff_2 (
    .J(j_k_ff_1_q), .clk(and_19_out), .K(j_k_ff_1_q), .Q(j_k_ff_2_q), .Qn(j_k_ff_2_qn), .reset(and_2_out));  // open: preset, en
  LED led_3 (.in(j_k_ff_3_q));
  J_K_Flip_Flop j_k_ff_3 (
    .J(or_2_out), .clk(and_19_out), .K(and_3_out), .Q(j_k_ff_3_q), .Qn(j_k_ff_3_qn), .reset(and_2_out));  // open: preset, en
  LED led_4 (.in(j_k_ff_4_q));
  LED led_5 (.in(j_k_ff_5_q));
  J_K_Flip_Flop j_k_ff_4 (
    .J(and_6_out), .clk(and_19_out), .K(or_1_out), .Q(j_k_ff_4_q), .Qn(j_k_ff_4_qn), .reset(and_2_out));  // open: preset, en
  LED led_6 (.in(j_k_ff_6_q));
  J_K_Flip_Flop j_k_ff_5 (
    .J(and_14_out), .clk(and_19_out), .K(and_8_out), .Q(j_k_ff_5_q), .Qn(j_k_ff_5_qn), .reset(and_2_out));  // open: preset, en
  J_K_Flip_Flop j_k_ff_6 (
    .J(and_4_out), .clk(and_19_out), .K(and_5_out), .Q(j_k_ff_6_q), .Qn(j_k_ff_6_qn), .reset(and_2_out));  // open: preset, en
  and and_4 (and_4_out, j_k_ff_1_q, j_k_ff_2_q, j_k_ff_3_q, j_k_ff_4_q, j_k_ff_5_q, j_k_ff_6_qn);
  and and_5 (and_5_out, j_k_ff_1_q, j_k_ff_2_q, j_k_ff_3_qn, j_k_ff_4_q, j_k_ff_5_q, j_k_ff_6_q);
  and and_6 (and_6_out, j_k_ff_1_q, j_k_ff_2_q, j_k_ff_3_q);
  and and_7 (and_7_out, j_k_ff_1_q, j_k_ff_2_q, j_k_ff_4_q);
  xor xor_1 (xor_1_out, j_k_ff_6_q, j_k_ff_3_q);
  and and_8 (and_8_out, and_7_out, xor_1_out);
  and and_9 (and_9_out, j_k_ff_1_q, j_k_ff_2_q, j_k_ff_5_q, j_k_ff_6_q);
  and and_10 (and_10_out, j_k_ff_1_q, j_k_ff_2_q, j_k_ff_4_qn);
  and and_11 (and_11_out, j_k_ff_1_q, j_k_ff_2_q, j_k_ff_5_qn);
  and and_12 (and_12_out, j_k_ff_1_q, j_k_ff_2_q, j_k_ff_6_qn);
  LED led_7 (.in(j_k_ff_7_q));
  J_K_Flip_Flop j_k_ff_7 (
    .J(1'b1), .clk(and_1_out), .K(1'b1), .Q(j_k_ff_7_q), .reset(and_13_out));  // open: Qn, preset, en
  and and_13 (and_13_out, j_k_ff_10_q, j_k_ff_11_q);
  and and_14 (and_14_out, and_6_out, j_k_ff_4_q);
  or or_1 (or_1_out, and_6_out, and_9_out);
  or or_2 (or_2_out, and_10_out, and_11_out, and_12_out);
  LED led_8 (.in(j_k_ff_8_q));
  J_K_Flip_Flop j_k_ff_8 (
    .J(j_k_ff_7_q), .clk(and_1_out), .K(j_k_ff_7_q), .Q(j_k_ff_8_q), .reset(and_13_out));  // open: Qn, preset, en
  J_K_Flip_Flop j_k_ff_9 (
    .J(and_15_out), .clk(and_1_out), .K(and_15_out), .Q(j_k_ff_9_q), .reset(and_13_out));  // open: Qn, preset, en
  and and_15 (and_15_out, j_k_ff_7_q, j_k_ff_8_q);
  LED led_9 (.in(j_k_ff_9_q));
  J_K_Flip_Flop j_k_ff_10 (
    .J(and_18_out), .clk(and_1_out), .K(and_16_out), .Q(j_k_ff_10_q), .reset(and_13_out));  // open: Qn, preset, en
  LED led_10 (.in(j_k_ff_10_q));
  J_K_Flip_Flop j_k_ff_11 (
    .J(and_17_out), .clk(and_1_out), .K(and_16_out), .Q(j_k_ff_11_q), .Qn(j_k_ff_11_qn), .reset(and_13_out));  // open: preset, en
  LED led_11 (.in(j_k_ff_11_q));
  and and_16 (and_16_out, j_k_ff_7_q, j_k_ff_8_q, j_k_ff_9_q);
  and and_17 (and_17_out, and_16_out, j_k_ff_10_q);
  and and_18 (and_18_out, and_16_out, j_k_ff_11_qn);
  and and_19 (and_19_out, j_k_ff_17_q, j_k_ff_16_q, j_k_ff_15_q, j_k_ff_13_q, j_k_ff_12_q);
  and and_20 (and_20_out, j_k_ff_17_q, j_k_ff_16_q, j_k_ff_15_q, j_k_ff_14_q);
  and and_21 (and_21_out, j_k_ff_12_q, j_k_ff_13_q);
  Clock Clk (.out(Clk_out));
  LED led_12 (.in(j_k_ff_12_q));
  J_K_Flip_Flop j_k_ff_12 (
    .J(1'b1), .clk(Clk_out), .K(1'b1), .Q(j_k_ff_12_q), .Qn(j_k_ff_12_qn), .reset(and_20_out));  // open: preset, en
  LED led_13 (.in(j_k_ff_13_q));
  J_K_Flip_Flop j_k_ff_13 (
    .J(j_k_ff_12_q), .clk(Clk_out), .K(j_k_ff_12_q), .Q(j_k_ff_13_q), .Qn(j_k_ff_13_qn), .reset(and_20_out));  // open: preset, en
  LED led_14 (.in(j_k_ff_14_q));
  LED led_15 (.in(j_k_ff_15_q));
  J_K_Flip_Flop j_k_ff_14 (
    .J(or_4_out), .clk(Clk_out), .K(and_21_out), .Q(j_k_ff_14_q), .Qn(j_k_ff_14_qn), .reset(and_20_out));  // open: preset, en
  LED led_16 (.in(j_k_ff_16_q));
  J_K_Flip_Flop j_k_ff_15 (
    .J(and_24_out), .clk(Clk_out), .K(or_3_out), .Q(j_k_ff_15_q), .Qn(j_k_ff_15_qn), .reset(and_20_out));  // open: preset, en
  J_K_Flip_Flop j_k_ff_16 (
    .J(and_31_out), .clk(Clk_out), .K(and_26_out), .Q(j_k_ff_16_q), .Qn(j_k_ff_16_qn), .reset(and_20_out));  // open: preset, en
  LED led_17 (.in(j_k_ff_17_q));
  J_K_Flip_Flop j_k_ff_17 (
    .J(and_22_out), .clk(Clk_out), .K(and_23_out), .Q(j_k_ff_17_q), .Qn(j_k_ff_17_qn), .reset(and_20_out));  // open: preset, en
  and and_22 (and_22_out, j_k_ff_12_q, j_k_ff_13_q, j_k_ff_14_q, j_k_ff_15_q, j_k_ff_16_q, j_k_ff_17_qn);
  and and_23 (and_23_out, j_k_ff_12_q, j_k_ff_13_q, j_k_ff_14_qn, j_k_ff_15_q, j_k_ff_16_q, j_k_ff_17_q);
  and and_24 (and_24_out, j_k_ff_12_q, j_k_ff_13_q, j_k_ff_14_q);
  and and_25 (and_25_out, j_k_ff_12_q, j_k_ff_13_q, j_k_ff_15_q);
  xor xor_2 (xor_2_out, j_k_ff_17_q, j_k_ff_14_q);
  and and_26 (and_26_out, and_25_out, xor_2_out);
  and and_27 (and_27_out, j_k_ff_12_q, j_k_ff_13_q, j_k_ff_16_q, j_k_ff_17_q);
  and and_28 (and_28_out, j_k_ff_12_q, j_k_ff_13_q, j_k_ff_15_qn);
  and and_29 (and_29_out, j_k_ff_12_q, j_k_ff_13_q, j_k_ff_16_qn);
  and and_30 (and_30_out, j_k_ff_12_q, j_k_ff_13_q, j_k_ff_17_qn);
  and and_31 (and_31_out, and_24_out, j_k_ff_15_q);
  or or_3 (or_3_out, and_24_out, and_27_out);
  or or_4 (or_4_out, and_28_out, and_29_out, and_30_out);
endmodule
